# Fritzing sketch RFVplotter-TB6600 (saved by Fritzing 0.9.9b)
breadboards: 1

parts:
  Raspberry_Pi_1 = Raspberry Pi 3 [part_number=RPI-3-V1.2]
  M1 = Stepper Motor - Bipolar
  J1 = Basic Servo
  R1 = Resistor [tolerance=±5% resistance=1k power=0.25 package=THT]
  BLDC1 = BLDC [chip_label=BLDC package="SIP (Single Inline) [THT]"]
  ESC1 = ESC [package="SIP (Single Inline) [THT]"]
  TB6600 = IC, SIP package, 12 pins [chip_label=IC]
  TB6600_2 = IC, SIP package, 12 pins [chip_label=IC]
  M2 = Stepper Motor - Bipolar

nets:
  N1: Raspberry_Pi_1.GPIO4, TB6600.pin4
  GND: Raspberry_Pi_1.GND, J1.gnd, ESC1.GND, TB6600.pin3, TB6600.pin5, TB6600.pin11, TB6600_2.pin3, TB6600_2.pin5, TB6600_2.pin11
  N2: Raspberry_Pi_1.GPIO17, TB6600.pin6
  N3: Raspberry_Pi_1.GPIO27, R1.Pin_0
  N4: Raspberry_Pi_1.GPIO22, TB6600_2.pin6
  N5: Raspberry_Pi_1.GPIO12, ESC1.Signal
  N6: Raspberry_Pi_1.GPIO23, TB6600_2.pin4
  N7: M1.A, TB6600.pin7
  N8: M1.C, TB6600.pin8
  N9: M1.B, TB6600.pin9
  N10: M1.D, TB6600.pin10
  5V: J1.vcc
  N11: J1.pulse, R1.Pin_1
  N12: BLDC1.pin1, ESC1.M1
  N13: BLDC1.pin2, ESC1.M2
  N14: BLDC1.pin3, ESC1.M3
  12V: ESC1.+12V, TB6600.pin12, TB6600_2.pin12
  N15: TB6600_2.pin7, M2.A
  N16: TB6600_2.pin8, M2.C
  N17: TB6600_2.pin9, M2.B
  N18: TB6600_2.pin10, M2.D

notes:
  Wiring using TB6600 stepper motor drivers.
  Rev.-1.0
  Vplotter-Drawing Robot

custom parts:
  BLDC: Brushless dc motor
  ESC: Electronic speed controller (ESC).
