# Fritzing sketch RFVplotter-DRV8825-Perfboard-v1_1 (saved by Fritzing 0.9.9b)
perfboards: 1

parts:
  DRV_1 = DRV 8825 Stepper Motor Carrier, High Current [part_number="DRV 8825"]
  DRV_2 = DRV 8825 Stepper Motor Carrier, High Current [part_number="DRV 8825"]
  J2 = male pin header, 8 pins [form="♂ (male)"]
  J3 = male pin header, 3 pins [form="♂ (male)"]
  J4 = male pin header, 3 pins [form="♂ (male)"]
  J6 = male pin header, 4 pins [form="♂ (male)"]
  J5 = male pin header, 3 pins [form="♂ (male)"]
  J7 = screw terminal, 4 pins  # not connected
  J8 = male pin header, 2 pins [form="♂ (male)"]
  J9 = male pin header, 2 pins [form="♂ (male)"]
  J10 = male pin header, 2 pins [form="♂ (male)"]
  J11 = male pin header, 2 pins [form="♂ (male)"]
  J12 = male pin header, 2 pins [form="♂ (male)"]
  J13 = male pin header, 2 pins [form="♂ (male)"]
  J14 = male pin header, 2 pins [form="♂ (male)"]
  J15 = male pin header, 2 pins [form="♂ (male)"]
  J16 = male pin header, 2 pins [form="♂ (male)"]
  J17 = male pin header, 2 pins [form="♂ (male)"]
  C1 = Electrolytic Capacitor [capacitance=0.1mF voltage=16V package="100 mil [THT, electrolytic]"]  # not connected
  C2 = Electrolytic Capacitor [capacitance=0.1mF voltage=16V package="100 mil [THT, electrolytic]"]  # not connected
  IC1 = IC, SIP package, 4 pins [chip_label=DCDC]
  Raspberry_Pi_1 = Raspberry Pi 3 [part_number=RPI-3-V1.2]
  J18 = male pin header, 4 pins [form="♂ (male)"]
  J19 = male pin header, 3 pins [form="♂ (male)"]
  J20 = male pin header, 4 pins [form="♂ (male)"]  # not connected
  J21 = male pin header, 3 pins [form="♂ (male)"]  # not connected
  R1 = Resistor [tolerance=±5% resistance=1k power=0.25 package=THT]
  R2 = Resistor [tolerance=±5% resistance=1k power=0.25 package=THT]

nets:
  N1: DRV_1.MS1, J10.pin1
  N2: DRV_1.MS2, J9.pin1
  N3: DRV_1.MS3, J8.pin1
  N4: DRV_1.RESET, J14.pin1
  N5: DRV_1.SLEEP, J15.pin1
  N6: DRV_1.STEP, J5.pin2
  N7: DRV_1.OUT_2B, J2.pin4
  N8: DRV_1.OUT_2A, J2.pin3
  N9: DRV_1.OUT_1A, J2.pin2
  N10: DRV_2.MS1, J11.pin1
  N11: DRV_2.MS2, J12.pin1
  N12: DRV_2.MS3, J13.pin1
  N13: DRV_2.RESET, J16.pin1
  N14: DRV_2.SLEEP, J17.pin1
  N15: DRV_2.VOLTAGE_ST/_MT, IC1.pin1
  N16: DRV_2.OUT_2B, J2.pin8
  N17: DRV_2.OUT_2A, J2.pin7
  N18: DRV_2.OUT_1A, J2.pin6
  N19: DRV_2.OUT_1B, J2.pin5
  N20: J3.pin1, R1.Pin_0
  N21: J3.pin2, J4.pin2, J11.pin2, J15.pin2, IC1.pin4
  N22: J3.pin3, J4.pin3
  N23: J4.pin1, R2.Pin_0
  N24: J6.pin1, R1.Pin_1
  N25: J5.pin1, R2.Pin_1
  N26: Raspberry_Pi_1.GPIO4, J18.pin2
  N27: Raspberry_Pi_1.GPIO17, J19.pin2
  N28: Raspberry_Pi_1.GPIO22, J19.pin3
  N29: Raspberry_Pi_1.GPIO12, J19.pin1
  N30: Raspberry_Pi_1.GPIO23, J18.pin3
  N31: Raspberry_Pi_1.GPIO18, J18.pin1
  N32: Raspberry_Pi_1.GND, J18.pin4

notes:
  +5V Out
  GND
  +12V Inn
  Left
  Stepper
  Right
  BLDC
  Servo
  Servo-GPIO18
  Ldir-GPIO4
  Lstp-GPIO17
  Rdir-GPIO23
  Rstp-GPIO22
  BLDC-GPIO12
  100uF capasitors between Vmot-GND as close to driver as possible.
