# Fritzing sketch RFVplotter-DRV8825 (saved by Fritzing 0.9.9b)
breadboards: 1

parts:
  Raspberry_Pi_1 = Raspberry Pi 3 [part_number=RPI-3-V1.2]
  DRV_1 = DRV 8825 Stepper Motor Carrier, High Current [part_number="DRV 8825"]
  DRV_2 = DRV 8825 Stepper Motor Carrier, High Current [part_number="DRV 8825"]
  M1 = Stepper Motor - Bipolar
  M2 = Stepper Motor - Bipolar
  J1 = Basic Servo
  R1 = Resistor [tolerance=±5% resistance=1k power=0.25 package=THT]
  BLDC1 = BLDC [chip_label=BLDC package="SIP (Single Inline) [THT]"]
  ESC1 = ESC [package="SIP (Single Inline) [THT]"]
  C1 = Electrolytic Capacitor [capacitance=100µF voltage=20V package="100 mil [THT, electrolytic]"]
  C2 = Electrolytic Capacitor [capacitance=100µF voltage=20V package="100 mil [THT, electrolytic]"]

nets:
  N1: Raspberry_Pi_1.GPIO4, DRV_1.DIRECTION
  N2: Raspberry_Pi_1.GPIO17, DRV_1.STEP
  N3: Raspberry_Pi_1.GPIO27, R1.Pin_0
  N4: Raspberry_Pi_1.GPIO22, DRV_2.STEP
  GND: Raspberry_Pi_1.GND, DRV_1.GROUND_ST/_MT, DRV_1.GROUND_LOG, DRV_2.GROUND_ST/_MT, DRV_2.GROUND_LOG, J1.gnd, ESC1.GND, C1.-, C2.-
  N5: Raspberry_Pi_1.GPIO12, ESC1.Signal
  N6: Raspberry_Pi_1.GPIO23, DRV_2.DIRECTION
  5V: DRV_1.MS1, DRV_1.MS2, DRV_1.MS3, DRV_1.RESET, DRV_1.SLEEP, DRV_2.MS1, DRV_2.MS2, DRV_2.MS3, DRV_2.RESET, DRV_2.SLEEP, J1.vcc
  12V: DRV_1.VOLTAGE_ST/_MT, DRV_2.VOLTAGE_ST/_MT, ESC1.+12V, C1.+, C2.+
  N7: DRV_1.OUT_2B, M1.C
  N8: DRV_1.OUT_2A, M1.A
  N9: DRV_1.OUT_1A, M1.B
  N10: DRV_1.OUT_1B, M1.D
  N11: DRV_2.OUT_2B, M2.C
  N12: DRV_2.OUT_2A, M2.A
  N13: DRV_2.OUT_1A, M2.B
  N14: DRV_2.OUT_1B, M2.D
  N15: J1.pulse, R1.Pin_1
  N16: BLDC1.pin1, ESC1.M1
  N17: BLDC1.pin2, ESC1.M2
  N18: BLDC1.pin3, ESC1.M3

notes:
  Vplotter-Drawing Robot
  Wiring using DRV8825 stepper motor drivers
  Rev.-1.0

custom parts:
  BLDC: Brushless dc motor
  ESC: Electronic speed controller (ESC).
